// Logisim project cpu.circ as structural Verilog: 1 circuit, main circuit cpu
module cpu (
  input  clk,
  input  [31:0] Instruction,
  input  [31:0] MemReadData,
  output [31:0] MemAddress,
  output [31:0] ProgramCounter,
  output [31:0] ra,
  output [31:0] sp,
  output [31:0] t0,
  output [31:0] t1,
  output [31:0] t2,
  output [31:0] s0,
  output [31:0] s1,
  output [31:0] a0,
  output [3:0] MemWriteMask,
  output [31:0] MemWriteData
);

  wire control_logic_1_p2, control_logic_1_p3, control_logic_1_p5, control_logic_1_p6, undriven, undriven_2,
       undriven_3, undriven_5;
  wire [1:0] undriven_6;
  wire [2:0] control_logic_1_p4;
  wire [3:0] undriven_4;
  wire [31:0] adder_1_out, adder_2_out, DataFromReg, imm_gen_1_immediate, Instruction2, LoadData,
       multiplexer_1_out, multiplexer_2_out, multiplexer_3_out, multiplexer_4_out, regfile_1_readdata1,
       Stage2, WB;

  Adder #(.width(32)) adder_1 (.a(ProgramCounter), .b(32'h4), .out(adder_1_out));  // open: cin, cout
  Register #(.width(32)) PC (.D(multiplexer_1_out), .clk(clk), .Q(ProgramCounter));  // open: en, clr
  Multiplexer #(.width(32)) multiplexer_1 (
    .in0(adder_1_out), .in1(MemAddress), .out(multiplexer_1_out), .sel(control_logic_1_p2));
  Register #(.width(32)) register_1 (.D(ProgramCounter), .clk(clk), .Q(Stage2));  // open: en, clr
  Multiplexer #(.width(32)) multiplexer_2 (
    .in0(Instruction), .in1(32'h13), .out(multiplexer_2_out), .sel(control_logic_1_p2));
  Register #(.width(32)) register_2 (.D(multiplexer_2_out), .clk(clk), .Q(Instruction2));  // open: en, clr
  // control_logic control_logic_1: pin names not known; wires that end beside it: Instruction2, control_logic_1_p2, control_logic_1_p3, control_logic_1_p4, control_logic_1_p5, control_logic_1_p6
  regfile regfile_1 (
    .ReadIndex1(Instruction2[19:15]), .ReadIndex2(Instruction2[24:20]), .WriteIndex(Instruction2[11:7]),
    .WriteData(WB), .RegWEn(control_logic_1_p3), .clk(clk), .ra(ra), .sp(sp), .t0(t0), .t1(t1), .t2(t2),
    .s0(s0), .s1(s1), .a0(a0), .ReadData1(regfile_1_readdata1), .ReadData2(DataFromReg));
  imm_gen imm_gen_1 (.Instruction(Instruction2), .ImmSel(control_logic_1_p4), .Immediate(imm_gen_1_immediate));
  Multiplexer #(.width(32)) multiplexer_3 (
    .in0(DataFromReg), .in1(imm_gen_1_immediate), .out(multiplexer_3_out), .sel(undriven));
  Multiplexer #(.width(32)) multiplexer_4 (
    .in0(regfile_1_readdata1), .in1(Stage2), .out(multiplexer_4_out), .sel(undriven_3));
  alu alu_1 (.ALUResult(MemAddress), .A(multiplexer_4_out), .B(multiplexer_3_out), .ALUSel(undriven_4));
  branch_comp branch_comp_1 (
    .BrData1(regfile_1_readdata1), .BrData2(DataFromReg), .BrUn(undriven_2), .BrEq(control_logic_1_p5),
    .BrLt(control_logic_1_p6));
  Adder #(.width(32)) adder_2 (.a(32'h4), .b(Stage2), .out(adder_2_out));  // open: cin, cout
  Multiplexer #(.select(2), .width(32)) multiplexer_5 (
    .in0(adder_2_out), .in1(MemAddress), .in2(LoadData), .out(WB), .sel(undriven_6));  // open: in3
  partial_store partial_store_1 (
    .Instruction(Instruction2), .MemAddress(MemAddress), .DataFromReg(DataFromReg), .MemWEn(undriven_5),
    .MemWriteMask(MemWriteMask), .DataToMem(MemWriteData));
  partial_load partial_load_1 (
    .Instruction(Instruction2), .MemAddress(MemAddress), .DataFromMem(MemReadData), .DataToReg(LoadData));

  // Other names for the same wires on the sheet: ALUResult[31:0] = MemAddress

  // Notes on the sheet:
  //   To IMEM
  //   IMEM (do **NOT** move this)
  //   From IMEM
  //   Inputs/Outputs for testing. Do **NOT** move these.
  //   It is OK to move the PC, RegFile, ALU, MEM, Branch Comp, Imm Gen, Partial Load, Partial Store and Control Logic to wherever is most convenient for you when constructing your CPU, and to delete this text
  //   To DMEM
  //   DMEM (do **NOT** move this)
  //   From DMEM
endmodule
