// Logisim project regfile.circ as structural Verilog: 1 circuit, main circuit regfile
module regfile (
  input  [4:0] ReadIndex1,
  input  [4:0] ReadIndex2,
  input  [4:0] WriteIndex,
  input  [31:0] WriteData,
  input  RegWEn,
  input  clk,
  output [31:0] ra,
  output [31:0] sp,
  output [31:0] t0,
  output [31:0] t1,
  output [31:0] t2,
  output [31:0] s0,
  output [31:0] s1,
  output [31:0] a0,
  output [31:0] ReadData1,
  output [31:0] ReadData2
);

  wire WEn0, WEn1, WEn2, WEn3, WEn4, WEn5, WEn6, WEn7, WEn8, WEn9, WEn10, WEn11, WEn12, WEn13, WEn14, WEn15,
       WEn16, WEn17, WEn18, WEn19, WEn20, WEn21, WEn22, WEn23, WEn24, WEn25, WEn26, WEn27, WEn28, WEn29,
       WEn30, WEn31;
  wire [31:0] a1, a2, a3, a4, a5, a6, a7, gp, in0, in1, in2, in3, in4, in5, in6, in7, in8, in9, in10, in11,
       in12, in13, in14, in15, in16, in17, in18, in19, in20, in21, in22, in23, in24, in25, in26, in27, in28,
       in29, in30, in31, s2, s3, s4, s5, s6, s7, s8, s9, s10, s11, t3, t4, t5, t6, tp, y0;

  Demultiplexer #(.select(5), .width(32)) demultiplexer_1 (
    .out0(in0), .out1(in1), .out2(in2), .out3(in3), .out4(in4), .out5(in5), .out6(in6), .out7(in7),
    .out8(in8), .out9(in9), .out10(in10), .out11(in11), .out12(in12), .out13(in13), .out14(in14),
    .out15(in15), .out16(in16), .out17(in17), .out18(in18), .out19(in19), .out20(in20), .out21(in21),
    .out22(in22), .out23(in23), .out24(in24), .out25(in25), .out26(in26), .out27(in27), .out28(in28),
    .out29(in29), .out30(in30), .out31(in31), .in(WriteData), .sel(WriteIndex));
  Demultiplexer #(.select(5)) demultiplexer_2 (
    .out0(WEn0), .out1(WEn1), .out2(WEn2), .out3(WEn3), .out4(WEn4), .out5(WEn5), .out6(WEn6), .out7(WEn7),
    .out8(WEn8), .out9(WEn9), .out10(WEn10), .out11(WEn11), .out12(WEn12), .out13(WEn13), .out14(WEn14),
    .out15(WEn15), .out16(WEn16), .out17(WEn17), .out18(WEn18), .out19(WEn19), .out20(WEn20), .out21(WEn21),
    .out22(WEn22), .out23(WEn23), .out24(WEn24), .out25(WEn25), .out26(WEn26), .out27(WEn27), .out28(WEn28),
    .out29(WEn29), .out30(WEn30), .out31(WEn31), .in(RegWEn), .sel(WriteIndex));
  Multiplexer #(.select(5), .width(32)) multiplexer_1 (
    .in0(y0), .in1(ra), .in2(sp), .in3(gp), .in4(tp), .in5(t0), .in6(t1), .in7(t2), .in8(s0), .in9(s1),
    .in10(a0), .in11(a1), .in12(a2), .in13(a3), .in14(a4), .in15(a5), .in16(a6), .in17(a7), .in18(s2),
    .in19(s3), .in20(s4), .in21(s5), .in22(s6), .in23(s7), .in24(s8), .in25(s9), .in26(s10), .in27(s11),
    .in28(t3), .in29(t4), .in30(t5), .in31(t6), .out(ReadData1), .sel(ReadIndex1));
  Multiplexer #(.select(5), .width(32)) multiplexer_2 (
    .in0(y0), .in1(ra), .in2(sp), .in3(gp), .in4(tp), .in5(t0), .in6(t1), .in7(t2), .in8(s0), .in9(s1),
    .in10(a0), .in11(a1), .in12(a2), .in13(a3), .in14(a4), .in15(a5), .in16(a6), .in17(a7), .in18(s2),
    .in19(s3), .in20(s4), .in21(s5), .in22(s6), .in23(s7), .in24(s8), .in25(s9), .in26(s10), .in27(s11),
    .in28(t3), .in29(t4), .in30(t5), .in31(t6), .out(ReadData2), .sel(ReadIndex2));
  Register #(.width(32)) register_1 (.D(in0), .en(1'b0), .clk(clk), .Q(y0));  // open: clr
  Register #(.width(32)) register_2 (.D(in1), .en(WEn1), .clk(clk), .Q(ra));  // open: clr
  Register #(.width(32)) register_3 (.D(in2), .en(WEn2), .clk(clk), .Q(sp));  // open: clr
  Register #(.width(32)) register_4 (.D(in3), .en(WEn3), .clk(clk), .Q(gp));  // open: clr
  Register #(.width(32)) register_5 (.D(in4), .en(WEn4), .clk(clk), .Q(tp));  // open: clr
  Register #(.width(32)) register_6 (.D(in5), .en(WEn5), .clk(clk), .Q(t0));  // open: clr
  Register #(.width(32)) register_7 (.D(in6), .en(WEn6), .clk(clk), .Q(t1));  // open: clr
  Register #(.width(32)) register_8 (.D(in7), .en(WEn7), .clk(clk), .Q(t2));  // open: clr
  Register #(.width(32)) register_9 (.D(in8), .en(WEn8), .clk(clk), .Q(s0));  // open: clr
  Register #(.width(32)) register_10 (.D(in9), .en(WEn9), .clk(clk), .Q(s1));  // open: clr
  Register #(.width(32)) register_11 (.D(in10), .en(WEn10), .clk(clk), .Q(a0));  // open: clr
  Register #(.width(32)) register_12 (.D(in11), .en(WEn11), .clk(clk), .Q(a1));  // open: clr
  Register #(.width(32)) register_13 (.D(in12), .en(WEn12), .clk(clk), .Q(a2));  // open: clr
  Register #(.width(32)) register_14 (.D(in13), .en(WEn13), .clk(clk), .Q(a3));  // open: clr
  Register #(.width(32)) register_15 (.D(in14), .en(WEn14), .clk(clk), .Q(a4));  // open: clr
  Register #(.width(32)) register_16 (.D(in15), .en(WEn15), .clk(clk), .Q(a5));  // open: clr
  Register #(.width(32)) register_17 (.D(in16), .en(WEn16), .clk(clk), .Q(a6));  // open: clr
  Register #(.width(32)) register_18 (.D(in17), .en(WEn17), .clk(clk), .Q(a7));  // open: clr
  Register #(.width(32)) register_19 (.D(in18), .en(WEn18), .clk(clk), .Q(s2));  // open: clr
  Register #(.width(32)) register_20 (.D(in19), .en(WEn19), .clk(clk), .Q(s3));  // open: clr
  Register #(.width(32)) register_21 (.D(in20), .en(WEn20), .clk(clk), .Q(s4));  // open: clr
  Register #(.width(32)) register_22 (.D(in21), .en(WEn21), .clk(clk), .Q(s5));  // open: clr
  Register #(.width(32)) register_23 (.D(in22), .en(WEn22), .clk(clk), .Q(s6));  // open: clr
  Register #(.width(32)) register_24 (.D(in23), .en(WEn23), .clk(clk), .Q(s7));  // open: clr
  Register #(.width(32)) register_25 (.D(in24), .en(WEn24), .clk(clk), .Q(s8));  // open: clr
  Register #(.width(32)) register_26 (.D(in25), .en(WEn25), .clk(clk), .Q(s9));  // open: clr
  Register #(.width(32)) register_27 (.D(in26), .en(WEn26), .clk(clk), .Q(s10));  // open: clr
  Register #(.width(32)) register_28 (.D(in27), .en(WEn27), .clk(clk), .Q(s11));  // open: clr
  Register #(.width(32)) register_29 (.D(in28), .en(WEn28), .clk(clk), .Q(t3));  // open: clr
  Register #(.width(32)) register_30 (.D(in29), .en(WEn29), .clk(clk), .Q(t4));  // open: clr
  Register #(.width(32)) register_31 (.D(in30), .en(WEn30), .clk(clk), .Q(t5));  // open: clr
  Register #(.width(32)) register_32 (.D(in31), .en(WEn31), .clk(clk), .Q(t6));  // open: clr

  // Notes on the sheet:
  //   INPUTS to your circuit
  //   DON'T CHANGE THE LOCATIONS OF THE INPUTS AND OUTPUTS!
  //   These are DEBUG/TEST outputs from your circuit.
  //   OUTPUTS from your circuit
endmodule
